# Fritzing sketch ESP8266_LED (saved by Fritzing 0.9.2b)
breadboards: 1

parts:
  Adafruit_HUZZAH_ESP8266_Breakout1 = Adafruit HUZZAH ESP8266 Breakout [part_number=2471]
  LED1 = smd LED [color="Red (633nm)" package="0603 [SMD]"]
  R1 = Resistor [tolerance=±5% resistance=68 package="2512 [SMD]"]
  USBTTL1 = USB TTL Serial Cable

nets:
  GND: Adafruit_HUZZAH_ESP8266_Breakout1.GND, R1.Pin_1, USBTTL1.GND
  N1: Adafruit_HUZZAH_ESP8266_Breakout1.VBat, USBTTL1.5V
  N2: Adafruit_HUZZAH_ESP8266_Breakout1.#0, LED1.anode
  N3: LED1.cathode, R1.Pin_0
  N4: USBTTL1.RX, USBTTL1.TX
